// Logisim project Washing_Machine_UC_UE.circ as structural Verilog
module main (
  input  Clock,
  input  [2:0] Address_Mod_Auto,
  input  Address_Clatire,
  input  Address_Prespalare,
  input  [1:0] Address_Temperatura,
  input  [1:0] Address_Viteza,
  input  Selector_MUX,
  input  Reset,
  input  Start,
  input  Confirm,
  input  Door,
  output [3:0] Anodes,
  output [6:0] Chatodes,
  output Led_On_Off,
  output Led_Door
);

  wire frequency_divider_1_div_clk, uc_1_enable_counter, uc_1_enable_counter_1_min, uc_1_enable_rom,
       uc_1_enable_ssd, uc_1_end_message, uc_1_load_counter, uc_1_reset_counter_1_min, uc_1_selector_mux,
       ue_1_t0_counter, ue_1_t0_counter_1_min;

  Frequency_divider frequency_divider_1 (.clock(Clock), .div_clk(frequency_divider_1_div_clk));
  UC uc_1 (
    .Clock(frequency_divider_1_div_clk), .Reset(Reset), .Start(Start), .Confirm(Confirm), .Door(Door),
    .T0_Counter(ue_1_t0_counter), .T0_Counter_1_min(ue_1_t0_counter_1_min), .Led_On_Off(Led_On_Off),
    .Led_Door_Locked(Led_Door), .Enable_ROM(uc_1_enable_rom), .Enable_Counter(uc_1_enable_counter),
    .Enable_Counter_1_min(uc_1_enable_counter_1_min), .Selector_MUX(uc_1_selector_mux),
    .Load_Counter(uc_1_load_counter), .Enable_SSD(uc_1_enable_ssd), .End_Message(uc_1_end_message),
    .Reset_Counter_1_min(uc_1_reset_counter_1_min));
  UE ue_1 (
    .Address_Mod_Auto(Address_Mod_Auto), .Address_Clatire(Address_Clatire),
    .Address_Prespalare(Address_Prespalare), .Address_Temperatura(Address_Temperatura),
    .Address_Viteza(Address_Viteza), .Selector_MUX_Mod(Selector_MUX),
    .Selector_MUX_Counters(uc_1_selector_mux), .Clock(Clock), .Reset(Reset), .Enable_ROM(uc_1_enable_rom),
    .Enable_Counter(uc_1_enable_counter), .Enable_Counter_1_min(uc_1_enable_counter_1_min),
    .Load_Counter(uc_1_load_counter), .Enable_SSD(uc_1_enable_ssd), .End_Message(uc_1_end_message),
    .Reset_Counter_1_min(uc_1_reset_counter_1_min), .T0_Counter(ue_1_t0_counter),
    .T0_Counter_1_min(ue_1_t0_counter_1_min), .Anodes(Anodes), .Chatodes(Chatodes));
endmodule

// VHDL entity UC, as the project stores it:
LIBRARY ieee;
USE ieee.std_logic_1164.all;

ENTITY UC IS
  PORT (
  	Clock : IN std_logic;
  	Reset : IN std_logic;
  	Start : IN std_logic;
  	Confirm : IN std_logic;
  	Door : IN std_logic;
  	T0_Counter : IN std_logic;
  	T0_Counter_1_min : IN std_logic;
  	
  	Led_On_Off : OUT std_logic;
  	Led_Door_Locked : OUT std_logic;
  	Enable_ROM : OUT std_logic;
  	Enable_Counter : OUT std_logic;
  	Enable_Counter_1_min : OUT std_logic;
  	Selector_MUX : OUT std_logic;
  	Load_Counter : OUT std_logic;
  	Enable_SSD : OUT std_logic;
  	End_Message : OUT std_logic;
  	Reset_Counter_1_min : OUT std_logic
    );
END UC;

ARCHITECTURE TypeArchitecture OF UC IS

type State is (Idle, Wait_Confirm, Wait_Counter, Wait_Counter_1_min, End_State);
signal Current_State, Next_State : State;

BEGIN

	process(Clock, Reset)
	begin

		if Reset = '1' then
			Current_State <= Idle;
		elsif Clock'event and Clock = '1' then
			Current_State <= Next_State;
		end if;
		
	end process;

	process(Current_State, Clock, Reset, Start, Confirm, Door, T0_Counter, T0_Counter_1_min)
	begin

		Led_On_Off <= '0';
		Led_Door_Locked <= '0';
		Enable_Counter <= '0';
		Enable_Counter_1_min <= '0';
		Enable_SSD <= '0';
		Enable_ROM <= '0';
		Selector_MUX <= '0';
		Load_Counter <= '0';
		End_Message <= '0';
		Reset_Counter_1_min <= '0';

		case Current_State is
			when Idle =>
				if Start = '1' then
					Next_State <= Wait_Confirm;
				else
					Next_State <= Idle;
				end if;
			when Wait_Confirm =>
				Led_On_Off <= '1';
				Enable_ROM <= '1';
				Enable_Counter <= '1';
				Enable_SSD <= '1';
				Load_Counter <= '1';
				if Confirm = '1' and Door = '1' then
					Next_State <= Wait_Counter;
				else
					Next_State <= Wait_Confirm;
				end if;
			when Wait_Counter =>
				Led_On_Off <= '1';
				Enable_ROM <= '1';
				Enable_Counter <= '1';
				Enable_SSD <= '1';
				Led_Door_Locked <= '1';
				Load_Counter <= '0';
				if T0_Counter = '1' then 
					Next_State <= Wait_Counter_1_min;
				else
					Next_State <= Wait_Counter;
				end if;
			when Wait_Counter_1_min =>
				Led_On_Off <= '1';
				Enable_ROM <= '1';
				Enable_Counter <= '0';
				Enable_SSD <= '1';
				Led_Door_Locked <= '1';
				Load_Counter <= '0';
				Selector_MUX <= '1';
				Enable_Counter_1_min <= '1';
				if T0_Counter_1_min = '1' then 
					Next_State <= End_State;
				else
					Next_State <= Wait_Counter_1_min;
				end if;
			when End_State =>
				Led_On_Off <= '1';
				Enable_ROM <= '1';
				Enable_Counter <= '0';
				Enable_SSD <= '1';
				Led_Door_Locked <= '0';
				Load_Counter <= '0';
				Selector_MUX <= '1';
				End_Message <= '1';
				Enable_Counter_1_min <= '0';
				Reset_Counter_1_min <= '1';
				if Start = '0' then
					Next_State <= Idle;
				else 
					Next_State <= End_State;
				end if;
			when others =>
				Next_State <= Idle;
		end case;
				
				

	end process;


END TypeArchitecture;

// VHDL entity UE, as the project stores it:
LIBRARY ieee;
USE ieee.std_logic_1164.all;

ENTITY UE IS
  PORT (
  	Address_Mod_Auto : IN std_logic_vector (2 downto 0);
  	Address_Clatire : IN std_logic;
  	Address_Prespalare : IN std_logic;
  	Address_Temperatura : IN std_logic_vector (1 downto 0);
  	Address_Viteza : IN std_logic_vector (1 downto 0);
  	Selector_MUX_Mod : IN std_logic;
  	Selector_MUX_Counters : IN std_logic;
  	Clock : IN std_logic;
  	Reset : IN std_logic;
  	Enable_ROM : IN std_logic;
  	Enable_Counter : IN std_logic;
  	Enable_Counter_1_min : IN std_logic;
  	Load_Counter : IN std_logic;
  	Enable_SSD : IN std_logic;
  	End_Message : IN std_logic;
  	Reset_Counter_1_min : IN std_logic;

  	T0_Counter : OUT std_logic;
  	T0_Counter_1_min : OUT std_logic;
  	Anodes : OUT std_logic_vector (3 downto 0);
  	Chatodes : OUT std_logic_vector (6 downto 0)
    );
END UE;

ARCHITECTURE TypeArchitecture OF UE IS

COMPONENT ROM_Viteza IS
  PORT (
  	Address : IN std_logic_vector (1 downto 0);
  	Enable : IN std_logic;
  	Clock : IN std_logic;
  	Data : OUT std_logic_vector (5 downto 0)
    );
END COMPONENT;

COMPONENT ROM_Temperatura IS
  PORT (
  	Address : IN std_logic_vector (1 downto 0);
  	Enable : IN std_logic;
  	Clock : IN std_logic;
  	Data : OUT std_logic_vector (5 downto 0)
    );
END COMPONENT;

COMPONENT ROM_Prespalare IS
  PORT (
  	Address : IN std_logic;
  	Enable : IN std_logic;
  	Clock : IN std_logic;
  	Data : OUT std_logic_vector (5 downto 0)
    );
END COMPONENT;

COMPONENT ROM_Clatire_Suplimentara IS
  PORT (
  	Address : IN std_logic;
  	Enable : IN std_logic;
  	Clock : IN std_logic;
  	Data : OUT std_logic_vector (5 downto 0)
    );
END COMPONENT;

COMPONENT Full_Adder IS
  PORT (
  	Op1 : IN std_logic_vector (5 downto 0);
  	Op2 : IN std_logic_vector (5 downto 0);
  	Op3 : IN std_logic_vector (5 downto 0);
  	Op4 : IN std_logic_vector (5 downto 0);
  	Result : OUT std_logic_vector (5 downto 0)
    );
END COMPONENT;

COMPONENT ROM_Mod_Automat IS
  PORT (
  	Address : IN std_logic_vector (2 downto 0);
  	Enable : IN std_logic;
  	Clock : IN std_logic;
  	Data : OUT std_logic_vector (5 downto 0)
    );
END COMPONENT;

COMPONENT MUX_2_to_1 IS
  PORT (
  	I0 : IN std_logic_vector (5 downto 0);
  	Selector : IN std_logic;
  	I1 : IN std_logic_vector (5 downto 0);
  	Output : OUT std_logic_vector (5 downto 0)
    );
END COMPONENT;

COMPONENT Counter_n_bits IS
  PORT (
  	Parallel_Input : IN std_logic_vector (5 downto 0);
  	Load : IN std_logic;
  	Enable : IN std_logic; 
  	Reset : IN std_logic;
  	Clock : IN std_logic;
  	Data : OUT std_logic_vector (5 downto 0);
  	T0 : OUT std_logic
    );
END COMPONENT;

COMPONENT Counter_1_min IS
  PORT (
  	Enable : IN std_logic;
  	Reset : IN std_logic;
  	Clock : IN std_logic;
  	Data : OUT std_logic_vector (5 downto 0);
  	T0 : OUT std_logic
    );
END COMPONENT;

COMPONENT Binary_to_Digits IS
  PORT (
    Number : IN std_logic_vector (5 downto 0);
    End_Program : IN std_logic;
    Digit0, Digit1, Digit2, Digit3 : OUT std_logic_vector (3 downto 0)
  );
END COMPONENT;

COMPONENT Frequency_divider_1_sec IS
	PORT (
		clk : IN std_logic;
  	     clk1 : OUT std_logic
  	     );
END COMPONENT;

COMPONENT SSD_Controller IS
  PORT (
  	Clock : IN std_logic;
  	Enable : IN std_logic;
  	Digit0, Digit1, Digit2, Digit3 : IN std_logic_vector (3 downto 0);
  	Anodes : OUT std_logic_vector (3 downto 0);
  	Chatodes : OUT std_logic_vector (6 downto 0)
    );
END COMPONENT;

COMPONENT Frequency_divider IS
  PORT (clock : IN std_logic;
  	   div_clk : OUT std_logic);
END COMPONENT;

COMPONENT OR_GATE IS
  PORT (
  	I0, I1 : IN std_logic;
  	Output : OUT std_logic
    );
END COMPONENT;

SIGNAL Clock_Divided, Clock_1_min : std_logic;
SIGNAL Address_S0, Address_S1, Address_S2, Address_S3, Address_S4 : std_logic_vector (5 downto 0);
SIGNAL Result_Sum_S5 : std_logic_vector (5 downto 0);
SIGNAL Output_MUX_S6 : std_logic_vector (5 downto 0);
SIGNAL Data_Counter_S7 : std_logic_vector (5 downto 0);
SIGNAL Reset_S8 : std_logic;
SIGNAL Data_Counter_1_min_S9 : std_logic_vector (5 downto 0);
SIGNAL Output_MUX_Counters_S10 : std_logic_vector (5 downto 0);
SIGNAL Output_Digit0_S11, Output_Digit1_S12, Output_Digit2_S13, Output_Digit3_S14 : std_logic_vector (3 downto 0);


BEGIN

	C0 : Frequency_divider port map (Clock, Clock_Divided);
	C1 : Frequency_divider_1_sec port map (Clock, Clock_1_min);
	C2 : ROM_Mod_Automat port map (Address_Mod_Auto, Enable_ROM, Clock_Divided, Address_S0);
	C3 : ROM_Clatire_Suplimentara port map (Address_Clatire, Enable_ROM, Clock_Divided, Address_S1);
	C4 : ROM_Prespalare port map (Address_Prespalare, Enable_ROM, Clock_Divided, Address_S2);
	C5 : ROM_Temperatura port map (Address_Temperatura, Enable_ROM, Clock_Divided, Address_S3);
	C6 : ROM_Viteza port map (Address_Viteza, Enable_ROM, Clock_Divided, Address_S4);
	C7 : Full_Adder port map (Address_S1, Address_S2, Address_S3, Address_S4, Result_Sum_S5);
	C8 : MUX_2_to_1 port map (Address_S0, Selector_MUX_Mod, Result_Sum_S5, Output_MUX_S6);
	C10 : Counter_n_bits port map (Output_MUX_S6, Load_Counter, Enable_Counter, Reset, Clock_1_min, Data_Counter_S7, T0_Counter);
	C11 : OR_GATE port map (Reset, Reset_Counter_1_min, Reset_S8);
	C12 : Counter_1_min port map (Enable_Counter_1_min, Reset_S8, Clock_1_min, Data_Counter_1_min_S9, T0_Counter_1_min);
	C13 : MUX_2_to_1 port map (Data_Counter_S7, Selector_MUX_Counters, Data_Counter_1_min_S9, Output_MUX_Counters_S10);
	C14 : Binary_to_Digits port map (Output_MUX_Counters_S10, End_Message, Output_Digit0_S11, Output_Digit1_S12, Output_Digit2_S13, Output_Digit3_S14);
	C15 : SSD_Controller port map (Clock, Enable_SSD, Output_Digit0_S11, Output_Digit1_S12, Output_Digit2_S13, Output_Digit3_S14, Anodes, Chatodes);
	
	
	


END TypeArchitecture;

--------------------------------------

LIBRARY ieee;
USE ieee.std_logic_1164.all;
USE ieee.std_logic_unsigned.all;

ENTITY ROM_Viteza IS
  PORT (
  	Address : IN std_logic_vector (1 downto 0);
  	Enable : IN std_logic;
  	Clock : IN std_logic;
  	Data : OUT std_logic_vector (
5 downto 0)
    );
END ROM_Viteza;

ARCHITECTURE TypeArchitecture OF ROM_Viteza IS

type Matrix is array (0 to 3) of std_logic_vector (5 downto 0);
signal Memory : Matrix := ("000101", "001010", "001111", "000000");

BEGIN

	PROCESS(Clock, Enable, Address)
	BEGIN

	if Clock = '1' and Clock'event and Enable = '1' then
		Data <= Memory(conv_integer(Address));
	end if;

	END PROCESS;


END TypeArchitecture;

--------------------------------------------

LIBRARY ieee;
USE ieee.std_logic_1164.all;
USE ieee.std_logic_unsigned.all;

ENTITY ROM_Temperatura IS
  PORT (
  	Address : IN std_logic_vector (1 downto 0);
  	Enable : IN std_logic;
  	Clock : IN std_logic;
  	Data : OUT std_logic_vector (5 downto 0)
    );
END ROM_Temperatura;

ARCHITECTURE TypeArchitecture OF ROM_Temperatura IS

type Matrix is array (0 to 3) of std_logic_vector (5 downto 0);
signal Memory : Matrix := ("001111", "010100", "010110", "011001");

BEGIN

	PROCESS(Clock, Enable, Address)
	BEGIN

	if Clock = '1' and Clock'event and Enable = '1' then
		Data <= Memory(conv_integer(Address));
	end if;

	END PROCESS;


END TypeArchitecture;

-----------------------------------------

LIBRARY ieee;
USE ieee.std_logic_1164.all;


ENTITY ROM_Prespalare IS
  PORT (
  	Address : IN std_logic;
  	Enable : IN std_logic;
  	Clock : IN std_logic;
  	Data : OUT std_logic_vector (5 downto 0)
    );
END ROM_Prespalare;

ARCHITECTURE TypeArchitecture OF ROM_Prespalare IS

type Matrix is array (0 to 1) of std_logic_vector (5 downto 0);
signal Memory : Matrix := ("000000", "001010");

BEGIN

	PROCESS(Clock, Enable, Address)
	BEGIN

	if Clock = '1' and Clock'event and Enable = '1' then
		if Address = '0' then 
			Data <= Memory(0);
		elsif Address = '1' then
			Data <= Memory(1);
		end if;
	end if;

	END PROCESS;


END TypeArchitecture;


----------------------------------------------

LIBRARY ieee;
USE ieee.std_logic_1164.all;


ENTITY ROM_Clatire_Suplimentara IS
  PORT (
  	Address : IN std_logic;
  	Enable : IN std_logic;
  	Clock : IN std_logic;
  	Data : OUT std_logic_vector (5 downto 0)
    );
END ROM_Clatire_Suplimentara;

ARCHITECTURE TypeArchitecture OF ROM_Clatire_Suplimentara IS

type Matrix is array (0 to 1) of std_logic_vector (5 downto 0);
signal Memory : Matrix := ("000000", "001010");

BEGIN

	PROCESS(Clock, Enable, Address)
	BEGIN

	if Clock = '1' and Clock'event and Enable = '1' then
		if Address = '0' then 
			Data <= Memory(0);
		elsif Address = '1' then
			Data <= Memory(1);
		end if;
	end if;

	END PROCESS;


END TypeArchitecture;


-------------------------------------------


LIBRARY ieee;
USE ieee.std_logic_1164.all;
USE ieee.std_logic_unsigned.all;
USE ieee.std_logic_arith.all;

ENTITY Full_Adder IS
  PORT (
  	Op1 : IN std_logic_vector (5 downto 0);
  	Op2 : IN std_logic_vector (5 downto 0);
  	Op3 : IN std_logic_vector (5 downto 0);
  	Op4 : IN std_logic_vector (5 downto 0);
  	Result : OUT std_logic_vector (5 downto 0)
    );
END Full_Adder;


ARCHITECTURE TypeArchitecture OF Full_Adder IS

BEGIN

	Result <= Op1 + Op2 + Op3 +
 Op4;

END TypeArchitecture;

------------------------------------------

LIBRARY ieee;
USE ieee.std_logic_1164.all;
USE ieee.std_logic_unsigned.all;

ENTITY ROM_Mod_Automat IS
  PORT (
  	Address : IN std_logic_vector (2 downto 0);
  	Enable : IN std_logic;
  	Clock : IN std_logic;
  	Data : OUT std_logic_vector (5 downto 0)
    );
END ROM_Mod_Automat;

ARCHITECTURE TypeArchitecture OF ROM_Mod_Automat IS

type Matrix is array (0 to 7) of std_logic_vector (5 downto 0);
signal Memory : Matrix := ("101000", "101101", "110010", "110010", "110100", "000000", "000000", "000000");

BEGIN

	PROCESS(Clock, Address, Enable)
	BEGIN

	if Clock = '1' and Clock'event and Enable = '1' then
		Data <= Memory(conv_integer(Address));
	end if;

	END PROCESS;


END TypeArchitecture;

------------------------------------------

LIBRARY ieee;
USE ieee.std_logic_1164.all;

ENTITY MUX_2_to_1 IS
  PORT (
  	I0 : IN std_logic_vector (5 downto 0);
  	Selector : IN std_logic;
  	I1 : IN std_logic_vector (5 downto 0);
  	Output : OUT std_logic_vector (5 downto 0)
    );
END MUX_2_to_1;


ARCHITECTURE TypeArchitecture OF MUX_2_to_1 IS

BEGIN

	Output <= I0 when (Selector = '0') else
			I1 when (Selector = '1');

END TypeArchitecture;

-------------------------------------

LIBRARY ieee;
USE ieee.std_logic_1164.all;
USE ieee.std_logic_unsigned.all;
USE ieee.std_logic_arith.all;

ENTITY Counter_n_bits IS
  PORT (
  	Parallel_Input : IN std_logic_vector (5 downto 0);
  	Load : IN std_logic;
  	Enable : IN std_logic; 
  	Reset : IN std_logic;
  	Clock : IN std_logic;
  	Data : OUT std_logic_vector (5 downto 0);
  	T0 : OUT std_logic
    );
END Counter_n_bits;

ARCHITECTURE TypeArchitecture OF Counter_n_bits IS

signal Counter : std_logic_vector (5 downto 0) := "UUUUUU";

BEGIN

	PROCESS(Clock, Reset, Load)
	BEGIN 
	if Reset = '1' then 
		Counter <= "UUUUUU";
	elsif rising_edge(Clock) and Enable = '1' then
		if Load = '1' then
			Counter <= Parallel_Input;
		elsif Counter /= "000000" then
			Counter <= Counter - 1;
		end if;
	end if;

	END PROCESS;

	PROCESS(Counter)
	BEGIN
	if Counter = "000000" then
		T0 <= '1';
	else
		T0 <= '0';
	end if;

	END PROCESS;

	Data <= Counter;


END TypeArchitecture;

-------------------------------------------------------

LIBRARY ieee;
USE ieee.std_logic_1164.all;
USE ieee.std_logic_unsigned.all;
USE ieee.std_logic_arith.all;

ENTITY Counter_1_min IS
  PORT (
  	Enable : IN std_logic;
  	Reset : IN std_logic;
  	Clock : IN std_logic;
  	Data : OUT std_logic_vector (5 downto 0);
  	T0 : OUT std_logic
    );
END Counter_1_min;

ARCHITECTURE TypeArchitecture OF Counter_1_min IS

signal Counter : std_logic_vector (5 downto 0) := "111100";

BEGIN

	PROCESS(Clock, Enable, Reset)
	BEGIN

	if Reset = '1' then
		Counter <= "111100";
	elsif rising_edge(Clock) and Enable = '1' then
		if Counter /= "000000" then 
			Counter <= Counter - 1;
		end if;
	end if;

	END PROCESS;

	PROCESS(Counter)
	BEGIN

	if Counter = "000000" then
		T0 <= '1';
		--Counter <= "111100";
	else 
		T0 <= '0';
	end if;

	END PROCESS;

	Data <= Counter;

END TypeArchitecture;


-------------------------------------------

LIBRARY ieee;
USE ieee.std_logic_1164.all;
USE ieee.numeric_std.all;

ENTITY Binary_to_Digits IS
  PORT (
    Number : IN std_logic_vector (5 downto 0);
    End_Program : IN std_logic;
    Digit0, Digit1, Digit2, Digit3 : OUT std_logic_vector (3 downto 0)
  );
END Binary_to_Digits;

ARCHITECTURE TypeArchitecture OF Binary_to_Digits IS
BEGIN
  PROCESS(Number, End_Program)
    VARIABLE num_int : INTEGER := 0;
    VARIABLE ones, tens : INTEGER := 0;
  BEGIN

  	if End_Program = '0' then 
  	
	     num_int := to_integer(unsigned(Number)); 
	    
	     ones := num_int mod 10; 
	     tens := num_int / 10;  
	    
	     Digit0 <= std_logic_vector(to_unsigned(ones, 4)); 
	     Digit1 <= std_logic_vector(to_unsigned(tens, 4)); 
	     Digit2 <= "1101";
	     Digit3 <= "1101";
	     
	elsif End_Program = '1' then
	
		Digit0 <= "1010";
		Digit1 <= "1011";
		Digit2 <= "1100";
		Digit3 <= "1101";
		
	end if;

    
  END PROCESS;
  
END TypeArchitecture;


-----------------------------------

LIBRARY IEEE;
USE IEEE.STD_LOGIC_1164.ALL;
USE ieee.std_logic_unsigned.all;

entity Frequency_divider_1_sec is
port (clk : in std_logic;
       clk1 : out std_logic);
end Frequency_divider_1_sec;

architecture BEHAVIORAL of Frequency_divider_1_sec is
	signal count : integer :=0;
	signal b : std_logic :='0';
	begin
	process(clk) 
	begin
	if(rising_edge(clk)) then
	count <=count+1;
	if(count = 50000000) then
	b <= not b;
	count <=0;
	end if;
	end if;
	clk1<=b;
	end process;
end BEHAVIORAL;


----------------------------------------

LIBRARY ieee;
USE ieee.std_logic_1164.all;

ENTITY SSD_Controller IS
  PORT (
  	Clock : IN std_logic;
  	Enable : IN std_logic;
  	Digit0, Digit1, Digit2, Digit3 : IN std_logic_vector (3 downto 0);
  	Anodes : OUT std_logic_vector (3 downto 0);
  	Chatodes : OUT std_logic_vector (6 downto 0)
    );
END SSD_Controller;

ARCHITECTURE TypeArchitecture OF SSD_Controller IS

COMPONENT Counter_16_bits is
    port (
        clock   : in std_logic;
        vector_out : out std_logic_vector(15 downto 0)
    );
END COMPONENT;

COMPONENT BCD_to_SSD IS
  PORT (
  	vector_in : IN std_logic_vector (3 downto 0);
  	vector_out : OUT std_logic_vector (6 downto 0)
    );
END COMPONENT;

COMPONENT Digits_MUX_4_to_1 IS
  PORT (
  	I0, I1, I2, I3 : IN std_logic_vector (3 downto 0);
  	Selector : IN std_logic_vector (1 downto 0);
  	Output : OUT std_logic_vector (3 downto 0)
    );
END COMPONENT;

COMPONENT SSD_MUX_4_to_1 IS
  PORT (
  	Enable : IN std_logic;
  	Selector : IN std_logic_vector (1 downto 0);
  	Output : OUT std_logic_vector (3 downto 0)
    );
END COMPONENT;

SIGNAL S0 : std_logic_vector (15 downto 0);
SIGNAL S1 : std_logic_vector (3 downto 0);

BEGIN

	C0 : Counter_16_bits port map (Clock, S0);
	C1 : Digits_MUX_4_to_1 port map (Digit0, Digit1, Digit2, Digit3, S0 (15 downto 14), S1);
	C2 : SSD_MUX_4_to_1 port map (Enable, S0 (15 downto 14), Anodes);
	C3 : BCD_to_SSD port map (S1, Chatodes);


END TypeArchitecture;

----------------------------------------------------------

library ieee;
use ieee.std_logic_1164.all;
use ieee.numeric_std.all;

entity Counter_16_bits is
    port (
        clock   : in std_logic;
        vector_out : out std_logic_vector(15 downto 0)
    );
end entity Counter_16_bits;

architecture Behavioral of Counter_16_bits is

    signal count : unsigned(15 downto 0);

begin

    process(clock)
    begin
        if rising_edge(clock) then
            if count = "1111111111111111" then
                count <= (others => '0');
            else
                count <= count + 1; 
            end if;
        end if;
    end process;

    vector_out <= std_logic_vector(count);

end architecture Behavioral;

--------------------------------------------------------------


LIBRARY ieee;
USE ieee.std_logic_1164.all;

ENTITY BCD_to_SSD IS
  PORT (
  	vector_in : IN std_logic_vector (3 downto 0);
  	vector_out : OUT std_logic_vector (6 downto 0)
    );
END BCD_to_SSD;

ARCHITECTURE TypeArchitecture OF BCD_to_SSD IS

BEGIN
	PROCESS(vector_in)
	BEGIN
	
		case vector_in is
			  when "0000" => vector_out <= "0111111"; 
	            when "0001" => vector_out <= "0000110"; 
	            when "0010" => vector_out <= "1011011"; 
	            when "0011" => vector_out <= "1001111"; 
	            when "0100" => vector_out <= "1100110"; 
	            when "0101" => vector_out <= "1101101"; 
	            when "0110" => vector_out <= "1111101"; 
	            when "0111" => vector_out <= "0000111"; 
	            when "1000" => vector_out <= "1111111"; 
	            when "1001" => vector_out <= "1101111"; 
	            when "1010" => vector_out <= "1011110";
	            when "1011" => vector_out <= "1010100";
	            when "1100" => vector_out <= "1111001";
	            when "1101" => vector_out <= "0000000"; 
	            when others => vector_out <= "0000000"; 
	     end case;
	     
     END PROCESS;


END TypeArchitecture;


-------------------------------------------------------


LIBRARY ieee;
USE ieee.std_logic_1164.all;

ENTITY Digits_MUX_4_to_1 IS
  PORT (
  	I0, I1, I2, I3 : IN std_logic_vector (3 downto 0);
  	Selector : IN std_logic_vector (1 downto 0);
  	Output : OUT std_logic_vector (3 downto 0)
    );
END Digits_MUX_4_to_1;

ARCHITECTURE TypeArchitecture OF Digits_MUX_4_to_1 IS

BEGIN

	
	Output <= I0 when (Selector = "00") else
			I1 when (Selector = "01") else
			I2 when (Selector = "10") else 
			I3 when (Selector = "11");

END TypeArchitecture;


------------------------------------------------------------

LIBRARY ieee;
USE ieee.std_logic_1164.all;

ENTITY SSD_MUX_4_to_1 IS
  PORT (
  	Enable : IN std_logic;
  	Selector : IN std_logic_vector (1 downto 0);
  	Output : OUT std_logic_vector (3 downto 0)
    );
END SSD_MUX_4_to_1;

ARCHITECTURE TypeArchitecture OF SSD_MUX_4_to_1 IS

BEGIN 

	PROCESS(Enable, Selector)
	BEGIN

	if Enable = '1' then 

		if Selector = "00" then
			Output <= "0001";
		elsif Selector = "01" then 
			Output <= "0010";
		elsif Selector = "10" then
			Output <= "0100";
		elsif Selector = "11" then
			Output <= "1000";
		end if;

	elsif Enable = '0' then

		Output <= "0000";

	end if;

	END PROCESS;
	
END TypeArchitecture;

----------------------------------------------

LIBRARY ieee;
USE ieee.std_logic_1164.all;

USE ieee.std_logic_unsigned.all;

ENTITY Frequency_divider IS
  PORT (clock : IN std_logic;
  	   div_clk : OUT std_logic);
END Frequency_divider;

ARCHITECTURE TypeArchitecture OF Frequency_divider IS

signal tmp: std_logic_vector ( 6 downto 0) := (others => '0');
BEGIN


process(clock)
BEGIN
	if(rising_edge(clock)) then
		if tmp = ("1100011") then tmp <= "0000000";
			elsif ( tmp <= "0110001") then
				tmp <= tmp + 1;
				div_clk <= '0';
			else div_clk <= '1';
				tmp <= tmp + 1;
		end if;
	end if;
end process;


END TypeArchitecture;

-------------------------------------------

LIBRARY ieee;
USE ieee.std_logic_1164.all;

ENTITY OR_GATE IS
  PORT (
  	I0, I1 : IN std_logic;
  	Output : OUT std_logic
    );
END OR_GATE;

ARCHITECTURE TypeArchitecture OF OR_GATE IS

BEGIN

	Output <= I0 or I1;

END TypeArchitecture;

// VHDL entity Frequency_divider, as the project stores it:
LIBRARY ieee;
USE ieee.std_logic_1164.all;

USE ieee.std_logic_unsigned.all;

ENTITY Frequency_divider IS
  PORT (clock : IN std_logic;
  	   div_clk : OUT std_logic);
END Frequency_divider;

ARCHITECTURE TypeArchitecture OF Frequency_divider IS

signal tmp: std_logic_vector ( 6 downto 0) := (others => '0');
BEGIN


process(clock)
BEGIN
	if(rising_edge(clock)) then
		if tmp = ("1100011") then tmp <= "0000000";
			elsif ( tmp <= "0110001") then
				tmp <= tmp + 1;
				div_clk <= '0';
			else div_clk <= '1';
				tmp <= tmp + 1;
		end if;
	end if;
end process;


END TypeArchitecture;
